# Fritzing sketch Needles in Ultrasound - Electronics Wiring Fritzing Diagram (saved by Fritzing 0.9.3b)
breadboards: 1

parts:
  M1 = Stepper Motor - Bipolar
  Arduiono_Uno_R3 = Arduino Uno (Rev3)
  J1 = male pin header, 10 pins [form="♂ (male)"]
  J2 = male pin header, 4 pins [form="♂ (male)"]
  J3 = male pin header, 2 pins [form="♂ (male)"]
  J4 = male pin header, 3 pins [form="♂ (male)"]
  J5 = male pin header, 5 pins [form="♂ (male)"]
  J6 = female pin header, 2 pins [form="♀ (female)"]
  J7 = female pin header, 2 pins [form="♀ (female)"]
  RE1 = Rotary Encoder [package=THT]
  R1 = Resistor [tolerance=±5% resistance=470 package=THT]
  R2 = Resistor [tolerance=±5% resistance=10k package=THT]
  J8 = female pin header, 1 pin [form="♀ (female)"]
  J9 = female pin header, 1 pin [form="♀ (female)"]

nets:
  N1: M1.A, J2.pin1
  N2: M1.C, J2.pin2
  N3: M1.B, J2.pin3
  N4: M1.D, J2.pin4
  N5: Arduiono_Uno_R3.A4/SDA, J7.pin1
  N6: Arduiono_Uno_R3.A5/SCL, J7.pin2
  N7: Arduiono_Uno_R3.D8, J1.pin9
  N8: Arduiono_Uno_R3.D9_PWM, J1.pin10
  N9: Arduiono_Uno_R3.D10_PWM/SS, J1.pin1
  N10: Arduiono_Uno_R3.D2, J4.pin3, RE1.EncoderPinB
  N11: Arduiono_Uno_R3.D3_PWM, J4.pin1, RE1.EncoderPinA
  N12: Arduiono_Uno_R3.D4, J5.pin3, R2.Pin_1
  N13: Arduiono_Uno_R3.D5_PWM, J5.pin1
  N14: Arduiono_Uno_R3.D6_PWM, J5.pin2
  N15: Arduiono_Uno_R3.D7, J5.pin4
  N16: Arduiono_Uno_R3.5V, J6.pin1, R1.Pin_1
  N17: Arduiono_Uno_R3.GND, J3.pin1, J4.pin2, J6.pin2, RE1.EncoderPinC, R2.Pin_0, J8.pin1
  N18: J1.pin5, J1.pin6, J1.pin7
  N19: J3.pin2, J9.pin1
  N20: J5.pin5, R1.Pin_0

notes:
  Big Easy Stepper
  Rotary Encoder
  Olimex 16x2 LCD and 4-button shield
  USB to computer
  Motor Power Supply
  Stepper Motor
